// Logisim project UART.circ as structural Verilog: 4 circuits, main circuit main
module main (
  input  [7:0] PacketInput,
  input  in_2,
  output [7:0] RecievedOutput
);

  wire clock_1_out, clock_2_out, Delay1_carry, enabler, Enabler_q, register_1_q, register_2_q, tx_1_dout;

  Counter #(.max('hf), .width(4)) Delay1 (
    .load(1'b0), .up(1'b1), .clk(clock_1_out), .carry(Delay1_carry));  // open: clr, count, D, Q
  Clock clock_1 (.out(clock_1_out));
  Register #(.width(1)) register_1 (.D(1'b1), .en(1'b1), .clk(Delay1_carry), .Q(register_1_q));  // open: clr
  Register #(.width(1)) register_2 (.D(tx_1_dout), .en(1'b1), .clk(enabler), .Q(register_2_q));  // open: clr
  TX tx_1 (.DIN(PacketInput), .RST(in_2), .DOUT(tx_1_dout));  // open: DOUT_VLD
  Clock clock_2 (.out(clock_2_out));
  Counter #(.max('hf), .width(4)) Delay2 (
    .load(1'b0), .up(1'b1), .count(register_1_q), .clk(clock_2_out), .carry(enabler));  // open: clr, D, Q
  RX rx_1 (.DIN(register_2_q), .enb(Enabler_q), .DOUT(RecievedOutput));  // open: RST, DOUT_VLD
  Register #(.width(1)) u_Enabler (.D(1'b1), .en(1'b1), .clk(enabler), .Q(Enabler_q));  // open: clr

  // Notes on the sheet:
  //   Delay Circuit
  //   Main Circuit
  //   Used to get a delay for reciever
  //   ------------------------------------------------------------------------------------------------------------------------------------------------------------------------------------------------------------------------------------------------------------------------------------------------------------------------------------------------
  //   Instructions
  //   2.Start the circuit by pressing 'ctrl+k'.
  //   3.You will recieve output in RecievedOutput
  //   1.Input the packet you want to send in PacketInput
endmodule

module FSM (
  input  DAT,
  input  CNT3,
  input  CNT4,
  input  CLK,
  input  RST,
  output RD,
  output CC3,
  output CC4,
  output VLD,
  output CLR
);

  wire and_1_out, and_2_out, and_3_out, and_4_out, and_5_out, not_1_out, or_1_out, shift_register_1_p2,
       shift_register_1_p12, shift_register_1_p13, shift_register_1_p15, shift_register_1_p16;

  not not_1 (not_1_out, DAT);
  and and_1 (and_1_out, shift_register_1_p12, not_1_out);
  and and_2 (and_2_out, CNT3, shift_register_1_p13);
  and and_3 (and_3_out, CNT3, CNT4, RD);
  and and_4 (and_4_out, CNT4, shift_register_1_p15);
  and and_5 (and_5_out, CNT3, shift_register_1_p16);
  or or_1 (or_1_out, and_1_out, and_2_out, and_3_out, and_4_out, and_5_out, VLD);
  // Shift_Register #(.length(6)) shift_register_1: pin names not known; wires that end beside it: RST, shift_register_1_p2, or_1_out, CLK, VLD, 1'b1, 1'b0, 1'b0, 1'b0, 1'b0, 1'b0, shift_register_1_p12, shift_register_1_p13, RD, shift_register_1_p15, shift_register_1_p16, VLD
  nor nor_1 (shift_register_1_p2, shift_register_1_p12, shift_register_1_p13, RD, shift_register_1_p15, shift_register_1_p16, VLD);
  or or_2 (CC3, shift_register_1_p13, RD, shift_register_1_p16);
  or or_3 (CC4, RD, shift_register_1_p15);
  nor nor_2 (CLR, RD, shift_register_1_p15, shift_register_1_p16, VLD);

  // Notes on the sheet:
  //   Data Input
  //   CNT3 Carry
  //   CNT4 Carry
  //   Clock Pulse
  //   Reset Input
  //   We are using this for controlling the enabler for our CNT3 and CNT4, using a shift register we are able to achieve it
  //   Finite State Machine
  //   Ready 
  //   DOUT_VLD
  //   Reset
  //   Enabler for CNT3
  //   Enabler for CNT4
endmodule

module RX (
  input  DIN,
  input  RST,
  input  enb,
  output [7:0] DOUT,
  output DOUT_VLD
);

  wire and_2_out, and_3_out, clk, clock_1_out, counter_1_carry, counter_2_carry, d_ff_1_q, d_ff_2_q,
       d_ff_3_q, d_ff_4_q, demultiplexer_1_out0, demultiplexer_1_out1, demultiplexer_1_out2,
       demultiplexer_1_out3, demultiplexer_1_out4, demultiplexer_1_out5, demultiplexer_1_out6,
       demultiplexer_1_out7, fsm_1_cc3, fsm_1_cc4, fsm_1_clr, fsm_1_rd, multiplexer_1_out, or_1_out,
       register_1_q, Timer_carry;
  wire [2:0] counter_2_q;

  Counter #(.max('hf), .width(4)) Timer (
    .load(1'b0), .up(1'b1), .clk(clk), .carry(Timer_carry));  // open: clr, count, D, Q
  Register #(.width(1)) register_1 (.D(DIN), .en(1'b1), .clk(Timer_carry), .Q(register_1_q));  // open: clr
  Clock clock_1 (.out(clock_1_out));
  and and_1 (clk, enb, clock_1_out);
  D_Flip_Flop d_ff_1 (.D(register_1_q), .clk(clk), .Q(d_ff_1_q), .preset(RST));  // open: Qn, reset
  D_Flip_Flop d_ff_2 (.D(d_ff_1_q), .clk(clk), .Q(d_ff_2_q), .preset(RST));  // open: Qn, reset
  D_Flip_Flop d_ff_3 (.D(counter_1_carry), .clk(clk), .Q(d_ff_3_q), .reset(RST));  // open: Qn, preset
  D_Flip_Flop d_ff_4 (.D(d_ff_2_q), .clk(clk), .Q(d_ff_4_q), .preset(RST));  // open: Qn, reset
  FSM fsm_1 (
    .DAT(d_ff_4_q), .CNT3(counter_2_carry), .CNT4(counter_1_carry), .CLK(clk), .RST(RST), .RD(fsm_1_rd),
    .CC3(fsm_1_cc3), .CC4(fsm_1_cc4), .VLD(DOUT_VLD), .CLR(fsm_1_clr));
  Multiplexer multiplexer_1 (.in0(clk), .in1(d_ff_3_q), .out(multiplexer_1_out), .sel(fsm_1_rd));
  Counter #(.max('hf), .width(4)) counter_1 (
    .clr(RST), .load(1'b0), .up(1'b1), .count(fsm_1_cc4), .clk(clk), .D(4'b0000), .carry(counter_1_carry));  // open: Q
  Counter #(.max('h7), .width(3)) counter_2 (
    .clr(RST), .load(1'b0), .up(1'b1), .count(fsm_1_cc3), .clk(multiplexer_1_out), .D(3'b000),
    .carry(counter_2_carry), .Q(counter_2_q));
  Demultiplexer #(.enable("true"), .select(3)) demultiplexer_1 (
    .out0(demultiplexer_1_out0), .out1(demultiplexer_1_out1), .out2(demultiplexer_1_out2),
    .out3(demultiplexer_1_out3), .out4(demultiplexer_1_out4), .out5(demultiplexer_1_out5),
    .out6(demultiplexer_1_out6), .out7(demultiplexer_1_out7), .in(d_ff_4_q), .sel(counter_2_q), .en(and_2_out));
  and and_2 (and_2_out, fsm_1_rd, counter_1_carry);
  and and_3 (and_3_out, fsm_1_clr, clk);
  or or_1 (or_1_out, RST, and_3_out);
  T_Flip_Flop t_ff_1 (.T(demultiplexer_1_out0), .clk(clk), .Q(DOUT[0]), .reset(or_1_out));  // open: Qn, preset
  T_Flip_Flop t_ff_2 (.T(demultiplexer_1_out2), .clk(clk), .Q(DOUT[2]), .reset(or_1_out));  // open: Qn, preset
  T_Flip_Flop t_ff_3 (.T(demultiplexer_1_out4), .clk(clk), .Q(DOUT[4]), .reset(or_1_out));  // open: Qn, preset
  T_Flip_Flop t_ff_4 (.T(demultiplexer_1_out6), .clk(clk), .Q(DOUT[6]), .reset(or_1_out));  // open: Qn, preset
  T_Flip_Flop t_ff_5 (.T(demultiplexer_1_out1), .clk(clk), .Q(DOUT[1]), .reset(or_1_out));  // open: Qn, preset
  T_Flip_Flop t_ff_6 (.T(demultiplexer_1_out3), .clk(clk), .Q(DOUT[3]), .reset(or_1_out));  // open: Qn, preset
  T_Flip_Flop t_ff_7 (.T(demultiplexer_1_out5), .clk(clk), .Q(DOUT[5]), .reset(or_1_out));  // open: Qn, preset
  T_Flip_Flop t_ff_8 (.T(demultiplexer_1_out7), .clk(clk), .Q(DOUT[7]), .reset(or_1_out));  // open: Qn, preset

  // Notes on the sheet:
  //   Reciever Circuit
  //   Synchronize the input
  //   Delay by one cycle
  //   G5 in CTR is Enable
  //   Allow only stable CLR
endmodule

module TX (
  input  [7:0] DIN,
  input  RST,
  output DOUT,
  output DOUT_VLD
);

  wire and_1_out, and_2_out, clock_1_out, clock_2_out, clock_3_out, clock_4_out, clock_5_out, clock_6_out,
       clock_7_out, clock_8_out, clock_9_out, counter_3_carry, counter_4_carry, d_ff_1_q, d_ff_2_q, d_ff_3_q,
       d_ff_4_q, DataTimer_carry, demultiplexer_1_out0, demultiplexer_1_out1, demultiplexer_1_out2,
       demultiplexer_1_out3, demultiplexer_1_out4, demultiplexer_1_out5, demultiplexer_1_out6,
       demultiplexer_1_out7, fsm_1_cc3, fsm_1_cc4, fsm_1_clr, fsm_1_rd, multiplexer_1_out, multiplexer_2_out,
       multiplexer_3_out, register_1_q, Reset, ret, undriven;
  wire [2:0] counter_2_q, counter_4_q;

  Counter #(.max('hf), .width(4)) DataTimer (
    .clr(undriven), .load(1'b0), .up(1'b1), .count(1'b1), .clk(clock_1_out), .carry(DataTimer_carry));  // open: D, Q
  Clock clock_1 (.out(clock_1_out));
  Counter #(.max('hf), .width(4)) counter_1 (
    .clr(RST), .load(1'b0), .up(1'b1), .clk(clock_2_out), .D(4'b0000), .carry(ret));  // open: count, Q
  Clock clock_2 (.out(clock_2_out));
  Counter #(.max('h7), .width(3)) counter_2 (
    .clr(RST), .load(1'b0), .up(1'b1), .clk(ret), .D(3'b000), .Q(counter_2_q));  // open: count, carry
  Register #(.width(1)) register_1 (
    .D(multiplexer_1_out), .en(1'b1), .clk(DataTimer_carry), .Q(register_1_q));  // open: clr
  Multiplexer #(.select(3)) multiplexer_1 (
    .in0(DIN[0]), .in1(DIN[1]), .in2(DIN[2]), .in3(DIN[3]), .in4(DIN[4]), .in5(DIN[5]), .in6(DIN[6]),
    .in7(DIN[7]), .out(multiplexer_1_out), .sel(counter_2_q));
  Clock clock_3 (.out(clock_3_out));
  Clock clock_4 (.out(clock_4_out));
  D_Flip_Flop d_ff_1 (.D(register_1_q), .clk(clock_3_out), .Q(d_ff_1_q), .preset(RST));  // open: Qn, reset
  D_Flip_Flop d_ff_2 (.D(counter_3_carry), .clk(clock_5_out), .Q(d_ff_2_q), .reset(RST));  // open: Qn, preset
  Clock clock_5 (.out(clock_5_out));
  D_Flip_Flop d_ff_3 (.D(d_ff_1_q), .clk(clock_3_out), .Q(d_ff_3_q), .preset(RST));  // open: Qn, reset
  D_Flip_Flop d_ff_4 (.D(d_ff_3_q), .clk(clock_3_out), .Q(d_ff_4_q), .preset(RST));  // open: Qn, reset
  FSM fsm_1 (
    .DAT(d_ff_4_q), .CNT3(counter_4_carry), .CNT4(counter_3_carry), .CLK(clock_4_out), .RST(RST),
    .RD(fsm_1_rd), .CC3(fsm_1_cc3), .CC4(fsm_1_cc4), .VLD(DOUT_VLD), .CLR(fsm_1_clr));
  Clock clock_6 (.out(clock_6_out));
  Clock clock_7 (.out(clock_7_out));
  Multiplexer multiplexer_2 (.in0(clock_7_out), .in1(d_ff_2_q), .out(multiplexer_2_out), .sel(fsm_1_rd));
  Counter #(.max('hf), .width(4)) counter_3 (
    .clr(RST), .load(1'b0), .up(1'b1), .count(fsm_1_cc4), .clk(clock_6_out), .D(4'b0000),
    .carry(counter_3_carry));  // open: Q
  Counter #(.max('h7), .width(3)) counter_4 (
    .clr(RST), .load(1'b0), .up(1'b1), .count(fsm_1_cc3), .clk(multiplexer_2_out), .D(3'b000),
    .carry(counter_4_carry), .Q(counter_4_q));
  Demultiplexer #(.enable("true"), .select(3)) demultiplexer_1 (
    .out0(demultiplexer_1_out0), .out1(demultiplexer_1_out1), .out2(demultiplexer_1_out2),
    .out3(demultiplexer_1_out3), .out4(demultiplexer_1_out4), .out5(demultiplexer_1_out5),
    .out6(demultiplexer_1_out6), .out7(demultiplexer_1_out7), .in(d_ff_4_q), .sel(counter_4_q), .en(and_1_out));
  and and_1 (and_1_out, fsm_1_rd, counter_3_carry);
  Clock clock_8 (.out(clock_8_out));
  or or_1 (Reset, RST, and_2_out);
  and and_2 (and_2_out, fsm_1_clr, clock_8_out);
  Multiplexer #(.select(3)) multiplexer_3 (
    .in0(demultiplexer_1_out0), .in1(demultiplexer_1_out1), .in2(demultiplexer_1_out2),
    .in3(demultiplexer_1_out3), .in4(demultiplexer_1_out4), .in5(demultiplexer_1_out5),
    .in6(demultiplexer_1_out6), .in7(demultiplexer_1_out7), .out(multiplexer_3_out), .sel(counter_4_q));
  Clock clock_9 (.out(clock_9_out));
  T_Flip_Flop t_ff_1 (.T(multiplexer_3_out), .clk(clock_9_out), .Q(DOUT), .reset(ret));  // open: Qn, preset

  // Notes on the sheet:
  //   Transmitter Circuit
  //   Synchronize the input
  //   RD=1 chains CTR4 and CTR3 into CTR7
  //   Delay by one cycle
  //   G5 in CTR is Enable
  //   Allow only stable CLR
endmodule
