// Logisim project alwsys.circ as structural Verilog: 5 circuits, main circuit main
module main (
  input  clk,
  input  resetn,
  input  uart_rxd,
  input  uart_rx_en,
  input  [7:0] recieveddata,
  input  in_6,
  input  [2:0] fsm_state,
  input  [2:0] n_fsm_state,
  output uart_rx_break,
  output uart_rx_valid,
  output [7:0] uart_rx_data
);

  wire comparator_1_eq, comparator_2_eq, comparator_3_eq, multiplexer_1_out, not_1_out, not_2_out,
       test2_1_out_2;
  wire [2:0] register_3_q, register_4_q;
  wire [7:0] register_1_q, register_2_q, undriven;

  Register register_1 (.D(recieveddata), .en(in_6), .clk(clk), .Q(register_1_q));  // open: clr
  Register register_2 (.D(undriven), .en(1'b1), .clk(clk), .Q(register_2_q));  // open: clr
  Register #(.width(3)) register_3 (.D(fsm_state), .en(in_6), .clk(clk), .Q(register_3_q));  // open: clr
  Register #(.width(3)) register_4 (.D(n_fsm_state), .en(in_6), .clk(clk), .Q(register_4_q));  // open: clr
  not not_1 (not_1_out, resetn);
  Comparator #(.width(3)) comparator_1 (.a(fsm_state), .b(3'b011), .eq(comparator_1_eq));  // open: gt, lt
  test2 test2_1 (.in_1(register_1_q), .out_2(test2_1_out_2));
  Comparator #(.width(3)) comparator_2 (.a(register_3_q), .b(3'b011), .eq(comparator_2_eq));  // open: gt, lt
  and and_1 (uart_rx_valid, comparator_2_eq, comparator_3_eq);
  Comparator #(.width(3)) comparator_3 (.a(register_4_q), .b(3'b000), .eq(comparator_3_eq));  // open: gt, lt
  and and_2 (uart_rx_break, test2_1_out_2, uart_rx_valid);
  Multiplexer multiplexer_1 (.in0(not_1_out), .in1(comparator_1_eq), .out(multiplexer_1_out), .sel(1'b0));
  Register register_5 (.D({8{1'b0}}), .en(multiplexer_1_out), .Q(uart_rx_data));  // open: clk, clr
  not not_2 (not_2_out, multiplexer_1_out);
  Register register_6 (.D(recieveddata), .en(not_2_out), .Q(uart_rx_data));  // open: clk, clr

  // Other names for the same wires on the sheet: asd[2:0] = fsm_state; rec[7:0] = recieveddata;
  //   tt[7:0] = uart_rx_data
endmodule

module test (
  input  D,
  output out_2
);

  wire clock_1_out;

  Clock #(.phaseOffset(1)) clock_1 (.out(clock_1_out));
  D_Flip_Flop d_ff_1 (.D(D), .clk(clock_1_out), .Q(out_2));  // open: Qn, preset, reset
endmodule

module test2 (
  input  [7:0] in_1,
  output out_2
);

  wire [7:0] or_1_out;

  assign or_1_out = in_1 | {8{1'b0}};  // OR_Gate or_1, 8 bits wide
  Comparator #(.mode("unsigned")) comparator_1 (.a(or_1_out), .b({8{1'b0}}), .eq(out_2));  // open: gt, lt
endmodule

module reg8 (
  input  inp,
  output outt
);

  wire clock_1_out;

  Clock clock_1 (.out(clock_1_out));
  D_Flip_Flop d_ff_1 (.D(inp), .clk(clock_1_out), .Q(outt));  // open: Qn, preset, reset
endmodule

module eightD (
  input  [7:0] in_1,
  input  in_2,
  input  [2:0] in_3,
  output out_4
);

  wire d_ff_1_q, d_ff_2_q, d_ff_3_q, d_ff_4_q, d_ff_5_q, d_ff_6_q, d_ff_7_q, d_ff_8_q, undriven, undriven_2,
       undriven_3, undriven_4, undriven_5, undriven_6, undriven_7;

  D_Flip_Flop d_ff_1 (.D(in_1[0]), .clk(in_2), .Q(d_ff_1_q), .reset(undriven));  // open: Qn, preset
  D_Flip_Flop d_ff_2 (.D(in_1[1]), .clk(in_2), .Q(d_ff_2_q), .preset(undriven), .reset(undriven_2));  // open: Qn
  D_Flip_Flop d_ff_3 (.D(in_1[2]), .clk(in_2), .Q(d_ff_3_q), .preset(undriven_2), .reset(undriven_3));  // open: Qn
  D_Flip_Flop d_ff_4 (.D(in_1[3]), .clk(in_2), .Q(d_ff_4_q), .preset(undriven_3), .reset(undriven_4));  // open: Qn
  D_Flip_Flop d_ff_5 (.D(in_1[4]), .clk(in_2), .Q(d_ff_5_q), .preset(undriven_4), .reset(undriven_5));  // open: Qn
  D_Flip_Flop d_ff_6 (.D(in_1[5]), .clk(in_2), .Q(d_ff_6_q), .preset(undriven_5), .reset(undriven_6));  // open: Qn
  D_Flip_Flop d_ff_7 (.D(in_1[6]), .clk(in_2), .Q(d_ff_7_q), .preset(undriven_6), .reset(undriven_7));  // open: Qn
  D_Flip_Flop d_ff_8 (.D(in_1[7]), .clk(in_2), .Q(d_ff_8_q), .preset(undriven_7));  // open: Qn, reset
  Multiplexer #(.select(3)) multiplexer_1 (
    .in0(d_ff_1_q), .in1(d_ff_2_q), .in2(d_ff_3_q), .in3(d_ff_4_q), .in4(d_ff_5_q), .in5(d_ff_6_q),
    .in6(d_ff_7_q), .in7(d_ff_8_q), .out(out_4), .sel(in_3));
endmodule
